# Fritzing sketch DIY Naze32 (saved by Fritzing 0.9.2b)
breadboards: 1

parts:
  U3 = STM32F103 [package=LQFP-48]
  GY1 = MPU-6050 Board GY-521 [form="♀ (female)" package=THT]
  BMP1 = BMP085 Breakout
  BREAKOUT1 = HMC5883L Compass Breakout

nets:
  N1: U3.PA0-WKUP, GY1.pin3, BMP1.SCL, BREAKOUT1.SCL
  N2: U3.PA1, GY1.pin4, BMP1.SDA, BREAKOUT1.SDA
  N3: GY1.pin1, BMP1.VIN
  GND: GY1.pin2, BMP1.GND, BREAKOUT1.GND

custom parts:
  MPU-6050 Board GY-521: Acelerometro y Giroscopio MPU-6050 Board GY-521
  BMP085 Breakout: A breakout for the BMP085 barometric pressure and temperature sensor
