# Fritzing sketch DIYGY-80 (saved by Fritzing 0.9.2b)
breadboards: 1

parts:
  Part1 = Triple Axis Accelerometer Breakout - ADXL345
  Part2 = Tri-Axis Gyro Breakout - L3G4200D
  BREAKOUT1 = HMC5883L Compass Breakout
  BMP1 = BMP085 Breakout

nets:
  GND: Part1.GND, Part2.GND, BREAKOUT1.GND, BMP1.GND
  VCC: Part1.VCC, Part2.VCC, BREAKOUT1.VIN, BMP1.VIN
  N1: Part1.SDA, Part2.SDA, BREAKOUT1.SDA, BMP1.SDA
  N2: Part1.SCL, Part2.SCL, BREAKOUT1.SCL, BMP1.SCL

custom parts:
  BMP085 Breakout: A breakout for the BMP085 barometric pressure and temperature sensor
