# Fritzing sketch DIYNaze32+OpenLRS (saved by Fritzing 0.9.2b)

parts:
  DIY_Naze32 = GY-80
  STM32 = STM32F103 [package=LQFP-48]
  920KV_Motor2 = DJI 920 KV Motor
  DJI_ESC_30A1 = DJI 30A ESC
  U2 = LIPO-2000mAh [package=lipo-2000]
  DIY_OpenLRS = Arduino Pro Mini v13
  U3 = RFM22 [package=rfm22-xxx-s2]

nets:
  N1: DIY_Naze32.VCC_IN, DIY_Naze32.VCC_3.3V, STM32.VDDA
  GND: DIY_Naze32.GND, STM32.VSSA, DJI_ESC_30A1.GND
  N2: DIY_Naze32.SCL, STM32.PB2, STM32.PB10
  N3: DIY_Naze32.SDA, DIY_Naze32.M_DRDY, STM32.PB11
  N4: STM32.VBAT, DJI_ESC_30A1.PWR_OUT
  N5: STM32.PA0-WKUP, DIY_OpenLRS.D9_PWM
  N6: STM32.PA8, STM32.PA9, DJI_ESC_30A1.DATA_OUT
  N7: 920KV_Motor2.w, DJI_ESC_30A1.W
  N8: 920KV_Motor2.u, DJI_ESC_30A1.U
  N9: DJI_ESC_30A1.GROUND, U2.-
  N10: DJI_ESC_30A1.+12V, U2.+
  N11: DIY_OpenLRS.GND, U3.SDN
  VCC: DIY_OpenLRS.VCC, U3.VCC
  N12: DIY_OpenLRS.D13/SCK, U3.SCLK
  N13: DIY_OpenLRS.D12/MISO, U3.SDO
  N14: DIY_OpenLRS.D11_PWM/MOSI, U3.SDI
  N15: DIY_OpenLRS.D2, U3.NIRQ

custom parts:
  DJI 920 KV Motor: DJI Brushless Outrunner 2212/920K Motor F330-550
