# Fritzing sketch DIYOpenLRS (saved by Fritzing 0.9.2b)

parts:
  U1 = RFM22 [package=rfm22-xxx-s2]
  Part1 = Arduino Pro Mini v13

nets:
  VCC: U1.VCC, Part1.VCC
  N1: U1.SDO, Part1.D12/MISO
  N2: U1.SDI, Part1.D11_PWM/MOSI
  N3: U1.SCLK, Part1.D13/SCK
  N4: U1.NIRQ, Part1.D2
  N5: U1.SDN, Part1.GND
