# Fritzing sketch GY-80Naze32 (saved by Fritzing 0.9.2b)

parts:
  Part1 = GY-80
  U1 = STM32F103 [package=LQFP-48]
  920KV_Motor2 = DJI 920 KV Motor
  DJI_ESC_30A1 = DJI 30A ESC
  U2 = LIPO-2000mAh [package=lipo-2000]

nets:
  N1: Part1.VCC_IN, Part1.VCC_3.3V, U1.VDDA
  GND: Part1.GND, U1.VSSA, DJI_ESC_30A1.GND
  N2: Part1.SCL, U1.PB2, U1.PB10
  N3: Part1.SDA, Part1.M_DRDY, U1.PB11
  N4: U1.VBAT, DJI_ESC_30A1.PWR_OUT
  N5: U1.PA8, U1.PA9, DJI_ESC_30A1.DATA_OUT
  N6: 920KV_Motor2.w, DJI_ESC_30A1.W
  N7: 920KV_Motor2.u, DJI_ESC_30A1.U
  N8: DJI_ESC_30A1.GROUND, U2.-
  N9: DJI_ESC_30A1.+12V, U2.+

custom parts:
  DJI 920 KV Motor: DJI Brushless Outrunner 2212/920K Motor F330-550
