# Fritzing sketch mega2560rc (saved by Fritzing 0.9.2b)
circuit board: 10cm x 5cm
breadboards: 1

parts:
  SwModel = Pushbutton [package=THT]
  SwMode = Pushbutton [package=THT]
  SwThrottle = Pushbutton [package=THT]
  SwRate = Pushbutton [package=THT]
  ConnectRF = screw terminal, 4 pins
  SwBind = Pushbutton [package=THT]
  R1 = Resistor [tolerance=±5% resistance=12k package=THT]
  R2 = Resistor [tolerance=±5% resistance=10k package=THT]
  R3 = Resistor [tolerance=±5% resistance=270 package=THT]
  LED1 = LED - 5mm [color="Red (633nm)" package="5 mm [THT]"]
  Sw1 = Pushbutton [package=THT]
  R4 = Resistor [tolerance=±5% resistance=47k package=THT]
  R5 = Resistor [tolerance=±5% resistance=47k package=THT]
  Piezo1 = Piezo Speaker
  R3_2 = Resistor [tolerance=±5% resistance=220 package=THT]
  U1 = Voltage Regulator - 5V [package="TO220 [THT]"]
  VCC = Battery block 9V
  SwMain = Pushbutton [package=THT]
  C2 = Ceramic Capacitor [capacitance=0.33µF package="100 mil [THT, multilayer]"]
  C1 = Ceramic Capacitor [capacitance=100nF package="100 mil [THT, multilayer]"]
  POT6 = Rotary Potentiometer (Small) [maximum_resistance=10kΩ package=THT]
  POT4 = Rotary Potentiometer (Small) [maximum_resistance=10kΩ package=THT]
  POT3 = Rotary Potentiometer (Small) [maximum_resistance=10kΩ package=THT]
  POT1 = Rotary Potentiometer (Small) [maximum_resistance=10kΩ package=THT]
  POT2 = Rotary Potentiometer (Small) [maximum_resistance=10kΩ package=THT]
  POT5 = Rotary Potentiometer (Small) [maximum_resistance=10kΩ package=THT]
  Part1 = Arduino Mega 2560 (Rev3)
  GLCD_128x1 = 128 x 64 Graphic LCD

nets:
  N1: SwModel.leg0, SwModel.leg1, SwMode.leg0, SwThrottle.leg0, SwRate.leg0, ConnectRF.pin4, SwBind.leg0, R2.Pin_0, R3.Pin_1, Sw1.leg0, R4.Pin_1, Piezo1.pin1, U1.GND, VCC.-, C2.0, C1.0, POT6.leg1, POT4.leg1, POT3.leg1, POT1.leg1, POT2.leg1, POT5.leg1
  N2: ConnectRF.pin1, R1.Pin_1, R2.Pin_1
  N3: ConnectRF.pin2, SwBind.leg1
  N4: ConnectRF.pin3, U1.output_voltage, C1.1, POT6.leg2, POT4.leg2, POT3.leg2, POT1.leg2, POT2.leg2, POT5.leg2
  N5: R3.Pin_0, LED1.cathode
  N6: R4.Pin_0, R5.Pin_1
  N7: R5.Pin_0, U1.input_voltage, SwMain.leg0, C2.1
  N8: Piezo1.pin2, R3_2.Pin_0
  N9: VCC.+, SwMain.leg1
  N10: POT6.wiper, Part1.A13
  N11: POT4.wiper, Part1.A11
  N12: POT3.wiper, Part1.A9
  N13: POT1.wiper, Part1.A8
  N14: POT2.wiper, Part1.A10
  N15: POT5.wiper, Part1.A12
  N16: Part1.5V, GLCD_128x1.1_Vss, GLCD_128x1.2_Vdd
  N17: Part1.D22, GLCD_128x1.7_DB0
  N18: Part1.D23, GLCD_128x1.8_DB1
  N19: Part1.D24, GLCD_128x1.9_BD2
  N20: Part1.D25, GLCD_128x1.10_DB3
  N21: Part1.D26, GLCD_128x1.11_DB4
  N22: Part1.D27, GLCD_128x1.12_DB5
  N23: Part1.D28, GLCD_128x1.13_DB6
  N24: Part1.D29, GLCD_128x1.14_DB7
  N25: Part1.D30, GLCD_128x1.5_R/W
  N26: Part1.D33, GLCD_128x1.17_RST
  N27: Part1.D34, GLCD_128x1.15_CS1

notes:
  Gnd
  +5v
  Bind
  PPM
  Arduino Radio Control
  6 channels RC transmitter
  http://www.reseau.org/arduinorc
  3 Sep 2013 - version 1.2
  Arduino Radio Control - 6 channels RC transmitter
  3 Sep 2013 - v 1.2 - http://www.reseau.org/arduinorc
